# Fritzing sketch aftertouch_glove (saved by Fritzing 0.7.4b)
breadboards: 1
perfboards: 1

parts:
  J1 = Infrared Proximity Sensor
  Part2 = Triple Axis Accelerometer Breakout - ADXL335
  S1 = Pushbutton [package="[THT]"]
  S2 = Pushbutton [package="[THT]"]
  S3 = Pushbutton [package="[THT]"]
  S4 = Pushbutton [package="[THT]"]
  Arduino1 = Arduino
  LED1 = Super Flux RGB LED (com. anode) [color=Blue]
  R1 = Resistor [tolerance=±5% resistance=220 package=THT]
  R2 = Resistor [tolerance=±5% resistance=220 package=THT]
  R3 = Resistor [tolerance=±5% resistance=220 package=THT]

nets:
  N1: J1.Vout, Arduino1.A5
  GND: J1.GND, Part2.GND, S1.Pin_1, S1.Pin_2, S2.Pin_1, S2.Pin_2, S3.Pin_1, S3.Pin_2, S4.Pin_1, S4.Pin_2, Arduino1.GND
  VCC: J1.Vcc, Arduino1.+5V
  N2: Part2.ZOUT, Arduino1.A2
  N3: Part2.YOUT, Arduino1.A1
  N4: Part2.XOUT, Arduino1.A0
  VCC_2: Part2.VCC, Arduino1.3V3
  N5: S1.Pin_3, S1.Pin_4, Arduino1.D10
  N6: S2.Pin_3, S2.Pin_4, Arduino1.D9
  N7: S3.Pin_3, S3.Pin_4, Arduino1.D8
  N8: S4.Pin_3, S4.Pin_4, Arduino1.D7
  N9: Arduino1.D6, R3.Pin_1
  N10: Arduino1.D5, R2.Pin_1
  N11: Arduino1.D3, R1.Pin_1
  N12: LED1.red_cathode, R3.Pin_0
  N13: LED1.blue_cathode, R2.Pin_0
  N14: LED1.green_cathode, R1.Pin_0

notes:
  to A8 on Teensy
  for Teensy
  R -> 5
  G -> 3
  B -> 4
  vcc 3V
